// Logisim project automat_bancar.circ as structural Verilog
module main (
  input  in_1,
  input  in_2,
  input  [3:0] NR_CARD,
  input  [15:0] PIN_CARD,
  input  [15:0] SUMA,
  input  [1:0] OPTIUNE,
  input  [15:0] PIN_NOU1,
  input  [15:0] PIN_NOU2,
  output [15:0] out_9,
  output PIN_INCORECT,
  output [15:0] out_11,
  output EROARE_RETRAGERE,
  output NU_COINCID,
  output [6:0] out_14,
  output [3:0] out_15
);

  wire clock_1_out, comparator_1000_1_egal, comparator_1000_1_mai_mic, comparator_pin_1_egal,
       comparator_pin_2_egal, comparator_sold_1_egal, comparator_sold_1_mai_mic, dmux_1_dout0, dmux_1_dout1,
       dmux_1_dout2, dmux_1_dout3, sau_2_intrari_1_y, sau_2_intrari_1_y_2, si_2_intrari_1_c, uc_1_afisor,
       uc_1_en_dmux, uc_1_en_scazator, uc_1_pin_en_comp, uc_1_pin_en_comp2, uc_1_sold_en_comp,
       uc_1_start_pin, uc_1_start_sold, uc_1_we1, uc_1_we2;
  wire [1:0] counter_1_bit_16_15;
  wire [3:0] mux_bcd_1_output;
  wire [15:0] scazator_sold_1_sold_nou;

  Clock clock_1 (.out(clock_1_out));
  uc uc_1 (
    .clock(in_1), .reset(in_2), .egal1(comparator_pin_1_egal), .egal2(comparator_pin_2_egal),
    .comparator_sold(si_2_intrari_1_c), .optiune1(dmux_1_dout0), .optiune2(dmux_1_dout1),
    .optiune3(dmux_1_dout2), .optiune4(dmux_1_dout3), .start_pin(uc_1_start_pin),
    .pin_en_comp(uc_1_pin_en_comp), .start_sold(uc_1_start_sold), .en_dmux(uc_1_en_dmux),
    .sold_en_comp(uc_1_sold_en_comp), .en_scazator(uc_1_en_scazator), .afisor(uc_1_afisor), .we1(uc_1_we1),
    .we2(uc_1_we2), .pin_en_comp2(uc_1_pin_en_comp2));
  dmux dmux_1 (
    .enable(uc_1_en_dmux), .sel(OPTIUNE), .dout0(dmux_1_dout0), .dout1(dmux_1_dout1), .dout2(dmux_1_dout2),
    .dout3(dmux_1_dout3));
  counter counter_1 (.clk(clock_1_out), .enable(uc_1_afisor), .R(in_2), .bit_16_15(counter_1_bit_16_15));
  mux_bcd mux_bcd_1 (
    .sel(counter_1_bit_16_15), .input0(out_11[3:0]), .input1(out_11[7:4]), .input2(out_11[11:8]),
    .input3(out_11[15:12]), .\output (mux_bcd_1_output));
  ram_pin ram_pin_1 (.NR_CARD(NR_CARD), .START(uc_1_start_pin), .WE(uc_1_we1), .PIN_NOU(PIN_NOU2), .PIN(out_9));
  ram_sold ram_sold_1 (
    .NR_CARD(NR_CARD), .START(uc_1_start_sold), .WE(uc_1_we2), .SOLD_NOU(scazator_sold_1_sold_nou),
    .SOLD(out_11));
  comparator_pin comparator_pin_2 (
    .ENABLE_COMP(uc_1_pin_en_comp2), .PIN_1(PIN_NOU1), .PIN_2(PIN_NOU2), .EGAL(comparator_pin_2_egal));
  mux_bcd mux_bcd_2 (
    .sel(counter_1_bit_16_15), .input0(4'b0001), .input1(4'b0010), .input2(4'b0100), .input3(4'b1000),
    .\output (out_15));
  BcdTo7Seg bcdto7seg_1 (.\input (mux_bcd_1_output), .seg(out_14));
  comparator_pin comparator_pin_1 (
    .ENABLE_COMP(uc_1_pin_en_comp), .PIN_1(out_9), .PIN_2(PIN_CARD), .EGAL(comparator_pin_1_egal));
  comparator_sold comparator_sold_1 (
    .ENABLE_COMP(uc_1_sold_en_comp), .SOLD_CURENT(out_11), .SOLD_RETRAS(SUMA), .EGAL(comparator_sold_1_egal),
    .MAI_MIC(comparator_sold_1_mai_mic));
  comparator_1000 comparator_1000_1 (
    .ENABLE_COMP(uc_1_sold_en_comp), .SOLD_RETRAS(SUMA), .EGAL(comparator_1000_1_egal),
    .MAI_MIC(comparator_1000_1_mai_mic));
  scazator_sold scazator_sold_1 (
    .ENABLE_SCAZATOR(uc_1_en_scazator), .SOLD_CURENT(out_11), .SOLD_RETRAS(SUMA),
    .SOLD_NOU(scazator_sold_1_sold_nou));
  assign PIN_INCORECT = uc_1_pin_en_comp ? ~comparator_pin_1_egal : 1'bz;  // Controlled_Inverter controlled_inverter_1
  assign NU_COINCID = uc_1_pin_en_comp2 ? ~comparator_pin_2_egal : 1'bz;  // Controlled_Inverter controlled_inverter_2
  _7_Segment_Display #(.active("false"), .decimalPoint("false")) u_7_segment_display_1 (
    .g(out_14[0]), .f(out_14[1]), .a(out_14[6]), .b(out_14[5]), .e(out_14[2]), .d(out_14[3]), .c(out_14[4]));
  SAU_2_INTRARI sau_2_intrari_1 (.A(comparator_sold_1_egal), .B(comparator_sold_1_mai_mic), .Y(sau_2_intrari_1_y));
  SAU_2_INTRARI sau_2_intrari_1_dup2 (
    .A(comparator_1000_1_egal), .B(comparator_1000_1_mai_mic), .Y(sau_2_intrari_1_y_2));
  _7_Segment_Display #(.active("false"), .decimalPoint("false")) u_7_segment_display_2 (
    .g(out_14[0]), .f(out_14[1]), .a(out_14[6]), .b(out_14[5]), .e(out_14[2]), .d(out_14[3]), .c(out_14[4]));
  _7_Segment_Display #(.active("false"), .decimalPoint("false")) u_7_segment_display_3 (
    .g(out_14[0]), .f(out_14[1]), .a(out_14[6]), .b(out_14[5]), .e(out_14[2]), .d(out_14[3]), .c(out_14[4]));
  _7_Segment_Display #(.active("false"), .decimalPoint("false")) u_7_segment_display_4 (
    .g(out_14[0]), .f(out_14[1]), .a(out_14[6]), .b(out_14[5]), .e(out_14[2]), .d(out_14[3]), .c(out_14[4]));
  SI_2_intrari si_2_intrari_1 (.a(sau_2_intrari_1_y), .b(sau_2_intrari_1_y_2), .c(si_2_intrari_1_c));
  assign EROARE_RETRAGERE = uc_1_sold_en_comp ? ~si_2_intrari_1_c : 1'bz;  // Controlled_Inverter controlled_inverter_3
endmodule

// VHDL entity ram_pin, as the project stores it:
--------------------------------------------------------------------------------
-- Project :
-- File    :
-- Autor   :
-- Date    :
--
--------------------------------------------------------------------------------
-- Description :
--
--------------------------------------------------------------------------------

LIBRARY ieee;
USE ieee.std_logic_1164.all;
USE ieee.numeric_std.all;


ENTITY ram_pin IS
  PORT (
  		NR_CARD: in std_logic_vector(3 downto 0);
  		START: in std_logic;
  		WE: in std_logic;
  		PIN: out std_logic_vector(15 downto 0);
  		PIN_NOU: in std_logic_vector(15 downto 0)
    );
END ram_pin;

--------------------------------------------------------------------------------
--Complete your VHDL description below
--------------------------------------------------------------------------------

ARCHITECTURE TypeArchitecture OF ram_pin IS

type MATRIX is array(0 to 15) of std_logic_vector(15 downto 0);
signal M: MATRIX :=(x"7589",x"4875",x"2248",x"3000",x"4000",x"0533",x"6849",x"7233",x"8134",x"0900",x"1643",x"0344",x"9845",x"7775",x"4398",x"3333");	
BEGIN

process(START,NR_CARD,WE)
begin
	case START is
	when '1' =>
		if WE = '0' then 
		case NR_CARD is
			when x"0" => PIN<=M(0);
			when x"1" => PIN<=M(1);
			when x"2" => PIN<=M(2);
			when x"3" => PIN<=M(3);
			when x"4" => PIN<=M(4);
			when x"5" => PIN<=M(5);
			when x"6" => PIN<=M(6);
			when x"7" => PIN<=M(7);
			when x"8" => PIN<=M(8);
			when x"9" => PIN<=M(9);
			when x"A" => PIN<=M(10);
			when x"B" => PIN<=M(11);
			when x"C" => PIN<=M(12);
			when x"D" => PIN<=M(13);
			when x"E" => PIN<=M(14);
			when x"F" => PIN<=M(15);
			when others => PIN<="ZZZZZZZZZZZZZZZZ";
		end case;
		end if;
	when others => 
		if WE = '1' then
		M(to_integer(unsigned(NR_CARD))) <= PIN_NOU;
		end if;
	end case;
end process;

END TypeArchitecture;

// VHDL entity ram_sold, as the project stores it:
--------------------------------------------------------------------------------
-- Project :
-- File    :
-- Autor   :
-- Date    :
--
--------------------------------------------------------------------------------
-- Description :
--
--------------------------------------------------------------------------------

LIBRARY ieee;
USE ieee.std_logic_1164.all;
USE ieee.numeric_std.all;

ENTITY ram_sold IS
  PORT (
  		NR_CARD: in std_logic_vector(3 downto 0);
  		START: in std_logic;
  		WE: in std_logic;
  		SOLD: out std_logic_vector(15 downto 0);
  		SOLD_NOU: in std_logic_vector(15 downto 0)
    );
END ram_sold;

--------------------------------------------------------------------------------
--Complete your VHDL description below
--------------------------------------------------------------------------------

ARCHITECTURE TypeArchitecture OF ram_sold IS

type MATRIX is array(0 to 15) of std_logic_vector(15 downto 0);
signal M: MATRIX :=(x"3000",x"3500",x"2500",x"3000",x"4000",x"0533",x"6849",x"7233",x"8134",x"0900",x"1643",x"0344",x"9845",x"7775",x"4398",x"3333");	
BEGIN

process(START,NR_CARD,WE,SOLD_NOU)
begin
	case START is
	when '1' =>
		if WE = '0' then 
		case NR_CARD is
			when x"0" => SOLD<=M(0);
			when x"1" => SOLD<=M(1);
			when x"2" => SOLD<=M(2);
			when x"3" => SOLD<=M(3);
			when x"4" => SOLD<=M(4);
			when x"5" => SOLD<=M(5);
			when x"6" => SOLD<=M(6);
			when x"7" => SOLD<=M(7);
			when x"8" => SOLD<=M(8);
			when x"9" => SOLD<=M(9);
			when x"A" => SOLD<=M(10);
			when x"B" => SOLD<=M(11);
			when x"C" => SOLD<=M(12);
			when x"D" => SOLD<=M(13);
			when x"E" => SOLD<=M(14);
			when x"F" => SOLD<=M(15);
			when others => SOLD<="ZZZZZZZZZZZZZZZZ";
		end case;
		elsif WE = '1' then 
		M(to_integer(unsigned(NR_CARD))) <= SOLD_NOU;
		end if;
	when others => SOLD <= "ZZZZZZZZZZZZZZZZ";
	end case;
end process;


END TypeArchitecture;

// VHDL entity comparator_pin, as the project stores it:
--------------------------------------------------------------------------------
-- Project :
-- File    :
-- Autor   :
-- Date    :
--
--------------------------------------------------------------------------------
-- Description :
--
--------------------------------------------------------------------------------

LIBRARY ieee;
USE ieee.std_logic_1164.all;

ENTITY comparator_pin IS
  PORT (
  		ENABLE_COMP: in std_logic;
  		PIN_1: in std_logic_vector (15 downto 0);
  		PIN_2: in std_logic_vector (15 downto 0);
  		EGAL: out std_logic
    );
END comparator_pin;

--------------------------------------------------------------------------------
--Complete your VHDL description below
--------------------------------------------------------------------------------

ARCHITECTURE TypeArchitecture OF comparator_pin IS

BEGIN
process(ENABLE_COMP,PIN_1,PIN_2)
begin

case ENABLE_COMP is
when '1' =>
	if PIN_1 = PIN_2 then
		EGAL <= '1';
	else
		EGAL <= '0';
	end if;
when others => EGAL <= '0';
end case;

end process;

END TypeArchitecture;

// VHDL entity comparator_sold, as the project stores it:
--------------------------------------------------------------------------------
-- Project :
-- File    :
-- Autor   :
-- Date    :
--
--------------------------------------------------------------------------------
-- Description :
--
--------------------------------------------------------------------------------

LIBRARY ieee;
USE ieee.std_logic_1164.all;

ENTITY comparator_sold IS
  PORT (
  		ENABLE_COMP: in std_logic;
  		SOLD_CURENT: in std_logic_vector (15 downto 0);
  		SOLD_RETRAS: in std_logic_vector (15 downto 0);
  		EGAL: out std_logic;
  		MAI_MIC: out std_logic
    );
END comparator_sold;

--------------------------------------------------------------------------------
--Complete your VHDL description below
--------------------------------------------------------------------------------

ARCHITECTURE TypeArchitecture OF comparator_sold IS

BEGIN
process(ENABLE_COMP,SOLD_CURENT,SOLD_RETRAS)
begin
MAI_MIC <= '0'; EGAL <= '0';
case ENABLE_COMP is
when '1' =>
	if SOLD_CURENT = SOLD_RETRAS then
		EGAL <= '1'; MAI_MIC <= '0';
	elsif SOLD_RETRAS < SOLD_CURENT then
		MAI_MIC <= '1'; EGAL <= '0';
	else
		MAI_MIC <= '0'; EGAL <= '0';
	end if;
when others => EGAL <= '0'; MAI_MIC <= '0';
end case;

end process;



END TypeArchitecture;

// VHDL entity SAU_2_INTRARI, as the project stores it:
--------------------------------------------------------------------------------
-- Project :
-- File    :
-- Autor   :
-- Date    :
--
--------------------------------------------------------------------------------
-- Description :
--
--------------------------------------------------------------------------------

LIBRARY ieee;
USE ieee.std_logic_1164.all;

ENTITY SAU_2_INTRARI IS
  PORT (
  		A: in std_logic;
  		B: in std_logic;
  		Y: out std_logic
    );
END SAU_2_INTRARI;

--------------------------------------------------------------------------------
--Complete your VHDL description below
--------------------------------------------------------------------------------

ARCHITECTURE TypeArchitecture OF SAU_2_INTRARI IS

BEGIN

Y <= A or B;

END TypeArchitecture;

// VHDL entity scazator_sold, as the project stores it:
--------------------------------------------------------------------------------
-- Project :
-- File    :
-- Autor   :
-- Date    :
--
--------------------------------------------------------------------------------
-- Description :
--
--------------------------------------------------------------------------------

LIBRARY ieee;
USE ieee.std_logic_1164.all;
use ieee.numeric_std.all;

ENTITY scazator_sold IS
  PORT (
  		ENABLE_SCAZATOR: in std_logic;
  		SOLD_CURENT: in std_logic_vector (15 downto 0);
  		SOLD_RETRAS: in std_logic_vector (15 downto 0);
  		SOLD_NOU: out std_logic_vector (15 downto 0)
    );
END scazator_sold;

--------------------------------------------------------------------------------
--Complete your VHDL description below
--------------------------------------------------------------------------------

ARCHITECTURE TypeArchitecture OF scazator_sold IS

BEGIN
process(ENABLE_SCAZATOR,SOLD_CURENT,SOLD_RETRAS)
begin

case ENABLE_SCAZATOR is 
when '1' =>
	SOLD_NOU <= std_logic_vector(signed(SOLD_CURENT) - signed(SOLD_RETRAS));
when others => SOLD_NOU <= x"0000";
end case;
end process;

END TypeArchitecture;

// VHDL entity dmux, as the project stores it:
--------------------------------------------------------------------------------
-- Project :
-- File    :
-- Autor   :
-- Date    :
--
--------------------------------------------------------------------------------
-- Description :
--
--------------------------------------------------------------------------------

LIBRARY ieee;
USE ieee.std_logic_1164.all;

ENTITY dmux IS
  PORT (
  		enable: in std_logic;
  		sel: in std_logic_vector (1 downto 0);
  		dout0, dout1, dout2, dout3: out std_logic
    );
END dmux;

--------------------------------------------------------------------------------
--Complete your VHDL description below
--------------------------------------------------------------------------------

ARCHITECTURE TypeArchitecture OF dmux IS

BEGIN
process (enable, sel)
begin
	case enable is
	when '1'=>
		case sel is
			when "00" => dout0 <= '1'; dout1 <= '0'; dout2 <= '0'; dout3 <= '0';
			when "01" => dout0 <= '0'; dout1 <= '1'; dout2 <= '0'; dout3 <= '0';
			when "10" => dout0 <= '0'; dout1 <= '0'; dout2 <= '1'; dout3 <= '0';
			when "11" => dout0 <= '0'; dout1 <= '0'; dout2 <= '0'; dout3 <= '1';
			when others =>dout0 <= '0'; dout1 <= '0'; dout2 <= '0'; dout3 <= '0';
		end case;
	when others=>
		dout0 <= '0'; dout1 <= '0'; dout2 <= '0'; dout3 <= '0';
	end case;
end process;
END TypeArchitecture;

// VHDL entity BcdTo7Seg, as the project stores it:
LIBRARY ieee;
USE ieee.std_logic_1164.all;

ENTITY BcdTo7Seg IS
  PORT (
  	input: in std_logic_vector (3 downto 0);
  	seg: out std_logic_vector (6 downto 0)
    	);
END BcdTo7Seg;

ARCHITECTURE TypeArchitecture OF BcdTo7Seg IS

BEGIN

	seg <= "0000001" when input = x"0" else
	 "1001111" when input = x"1" else
	 "0010010" when input = x"2" else
	 "0000110" when input = x"3" else
	 "1001100" when input = x"4" else
	 "0100100" when input = x"5" else
	 "0100000" when input = x"6" else
	 "0001111" when input = x"7" else
	 "0000000" when input = x"8" else
	 "0000100" when input = x"9" else
	 "0001000" when input = x"A" else
	 "1100000" when input = x"B" else
	 "0110000" when input = x"C" else
	 "1000010" when input = x"D" else
	 "0110000" when input = x"E" else
	 "0111000" when input = x"F" else
	 "1111111";
	

END TypeArchitecture;

// VHDL entity uc, as the project stores it:
--------------------------------------------------------------------------------
-- Project :
-- File    :
-- Autor   :
-- Date    :
--
--------------------------------------------------------------------------------
-- Description :
--
--------------------------------------------------------------------------------

LIBRARY ieee;
USE ieee.std_logic_1164.all;

ENTITY uc IS
  PORT (
  		clock, reset, egal1, egal2, comparator_sold, optiune1, optiune2, optiune3, optiune4: in std_logic;
  		start_pin, pin_en_comp, start_sold, en_dmux, sold_en_comp, en_scazator, afisor, we1, we2, pin_en_comp2: out std_logic
    );
END uc;

--------------------------------------------------------------------------------
--Complete your VHDL description below
--------------------------------------------------------------------------------

ARCHITECTURE TypeArchitecture OF uc IS
type STARE_T is(START, PIN_VERIF, ALEGERE_OPT, OPTIUNE_1, OPTIUNE_2, COMPARARE_SUMA, SUMA_RETRAGERE, OPTIUNE_3, SCHIMBARE_PIN, OPTIUNE_4);
signal STARE, NXSTARE: STARE_T;
BEGIN

ACTUALIZEAZA_STARE: process(reset, clock)
begin
	case reset is
	when '1' =>
		STARE <= START;
	when others=>
		if CLOCK = '1' and clock'event then
			STARE <= NXSTARE;
		end if;
	end case;
end process ACTUALIZEAZA_STARE;

TRANSITIONS: process (STARE, egal1, egal2, comparator_sold, optiune1, optiune2, optiune3, optiune4)
begin
--initializari
start_pin <= '0';
pin_en_comp <= '0';
start_sold <= '0';
en_dmux <= '0';
sold_en_comp <= '0';
en_scazator <= '0';
pin_en_comp <= '0';
afisor <= '0';
we1 <= '0';
we2 <= '0';
pin_en_comp2 <= '0';

case STARE is
	when START => start_pin <= '1'; pin_en_comp <= '0';
start_sold <= '0';
en_dmux <= '0';
sold_en_comp <= '0';
en_scazator <= '0';
pin_en_comp <= '0';
afisor <= '0';
we1 <= '0';
we2 <= '0';
pin_en_comp2 <= '0';
NXSTARE <= PIN_VERIF;
	when PIN_VERIF => start_pin <= '1'; pin_en_comp <= '1';
		if egal1 = '1' then NXSTARE <= ALEGERE_OPT;
		else NXSTARE <= START;
		end if;
	when ALEGERE_OPT => en_dmux <= '1';
		if optiune1 = '1' then NXSTARE <= OPTIUNE_1;
		elsif optiune2 = '1' then NXSTARE <= OPTIUNE_2;
		elsif optiune3 = '1' then NXSTARE <= OPTIUNE_3;
		elsif optiune4 = '1' then NXSTARE <= OPTIUNE_4;
		end if;
	when OPTIUNE_1 => start_sold <= '1'; afisor <= '1'; NXSTARE <= START;
	when OPTIUNE_2 => start_sold <= '1'; NXSTARE <= COMPARARE_SUMA;
	when COMPARARE_SUMA => start_sold <= '1'; sold_en_comp <= '1';
		if comparator_sold = '1' then NXSTARE <= SUMA_RETRAGERE;
		else NXSTARE <= OPTIUNE_2;
		end if;
	when SUMA_RETRAGERE => start_sold <= '1'; en_scazator <= '1'; we2 <= '1'; NXSTARE <= START;
	when OPTIUNE_3 => pin_en_comp2 <= '1'; 
		if egal2 = '1' then NXSTARE <= SCHIMBARE_PIN;
		else NXSTARE <= START;
		end if;
	when SCHIMBARE_PIN => we1 <= '1'; NXSTARE <= START;
	when OPTIUNE_4 => start_pin <= '1'; NXSTARE <= START;
end case;
end process;
END TypeArchitecture;

// VHDL entity comparator_1000, as the project stores it:
--------------------------------------------------------------------------------
-- Project :
-- File    :
-- Autor   :
-- Date    :
--
--------------------------------------------------------------------------------
-- Description :
--
--------------------------------------------------------------------------------

LIBRARY ieee;
USE ieee.std_logic_1164.all;

ENTITY comparator_1000 IS
  PORT (
  		ENABLE_COMP: in std_logic;
  		SOLD_RETRAS: in std_logic_vector (15 downto 0);
  		EGAL: out std_logic;
  		MAI_MIC: out std_logic
    );
END comparator_1000;

--------------------------------------------------------------------------------
--Complete your VHDL description below
--------------------------------------------------------------------------------

ARCHITECTURE TypeArchitecture OF comparator_1000 IS

BEGIN
process(ENABLE_COMP)
begin
MAI_MIC <= '0'; EGAL <= '0';
case ENABLE_COMP is 
when '1' =>
	if SOLD_RETRAS = x"03e8" then
		EGAL <= '1'; MAI_MIC <= '0';
	elsif SOLD_RETRAS < x"03e8" then
		MAI_MIC <= '1'; EGAL <= '0';
	else
		MAI_MIC <= '0'; EGAL <= '0';
	end if;
when others => MAI_MIC <= '0'; EGAL <= '0';
end case;

end process;



END TypeArchitecture;

// VHDL entity SI_2_intrari, as the project stores it:
--------------------------------------------------------------------------------
-- Project :
-- File    :
-- Autor   :
-- Date    :
--
--------------------------------------------------------------------------------
-- Description :
--
--------------------------------------------------------------------------------

LIBRARY ieee;
USE ieee.std_logic_1164.all;

ENTITY SI_2_intrari IS
  PORT ( a, b: in std_logic;
  c: out std_logic
    );
END SI_2_intrari;

--------------------------------------------------------------------------------
--Complete your VHDL description below
--------------------------------------------------------------------------------

ARCHITECTURE TypeArchitecture OF SI_2_intrari IS

BEGIN

c <= a and b;

END TypeArchitecture;

// VHDL entity counter, as the project stores it:
--------------------------------------------------------------------------------
-- Project :
-- File    :
-- Autor   :
-- Date    :
--
--------------------------------------------------------------------------------
-- Description :
--
--------------------------------------------------------------------------------

LIBRARY ieee;
USE ieee.std_logic_1164.all;
USE ieee.std_logic_UNSIGNED.all;

ENTITY counter IS
  PORT (
  	clk, enable: in std_logic;
  	R: in std_logic;
  	bit_16_15: out std_logic_vector(1 downto 0)
    );
END counter;

--------------------------------------------------------------------------------
--Complete your VHDL description below
--------------------------------------------------------------------------------

ARCHITECTURE comportamental OF counter IS

BEGIN

	process (clk, enable)
	variable count: std_logic_vector (16 downto 0) := "00000000000000000";
	begin
	case enable is
	when '1' =>
		if clk='1' and clk'event then
			if R = '0' then count := "00000000000000000";
			else
				count := count + 1999999999;
			end if;
		end if;
		bit_16_15 <= count(16) & count(15);
	when others => bit_16_15 <= "00";
	end case;
	end process;

END comportamental;

// VHDL entity mux_bcd, as the project stores it:
--------------------------------------------------------------------------------
-- Project :
-- File    :
-- Autor   :
-- Date    :
--
--------------------------------------------------------------------------------
-- Description :
--
--------------------------------------------------------------------------------

LIBRARY ieee;
USE ieee.std_logic_1164.all;

ENTITY mux_bcd IS
  PORT ( sel: in std_logic_vector(1 downto 0);
  input0, input1, input2, input3: in std_logic_vector(3 downto 0);
  output: out std_logic_vector(3 downto 0)
    );
END mux_bcd;

--------------------------------------------------------------------------------
--Complete your VHDL description below
--------------------------------------------------------------------------------

ARCHITECTURE TypeArchitecture OF mux_bcd IS

BEGIN

process(sel,input0,input1,input2,input3)
begin
	case sel is
	when "00" => output <= input0;
	when "01" => output <= input1;
	when "10" => output <= input2;
	when "11" => output <= input3;
	when others => output<="ZZZZ";
	end case;
end process;

END TypeArchitecture;
